// Logisim project tower_boards.circ as structural Verilog: 5 circuits, main circuit Tower
module Tower (
);

  wire CLK, RESET;
  wire [2:0] FLAGS;
  wire [7:0] DATA_BUS;
  wire [15:0] ADDRESS_BUS;
  wire [39:0] CONTROL;

  LED led_1 (.in(CLK));
  // LedBar #(.inputtype("row")) ledbar_1: pin names not known; wires that end beside it: DATA_BUS
  // LedBar #(.inputtype("row"), .matrixcols(16)) ledbar_2: pin names not known; wires that end beside it: ADDRESS_BUS
  Button u_RESET (.out(RESET));
  Board_4 ALU (
    .RESET(RESET), .CLK(CLK), .DATA_BUS_IN(DATA_BUS), .ADDRESS_BUS_IN(ADDRESS_BUS), .CONTROL_IN(CONTROL),
    .DATA_BUS_OUT(DATA_BUS), .ADDRESS_BUS_OUT(ADDRESS_BUS), .CONTROL_FLAGS_OUT(FLAGS));
  Board_3 Control_logic (
    .RESET(RESET), .CLK(CLK), .DATA_BUS_IN(DATA_BUS), .ADDRESS_BUS_IN(ADDRESS_BUS), .FLAGS_IN(FLAGS),
    .DATA_BUS_OUT(DATA_BUS), .ADDRESS_BUS_OUT(ADDRESS_BUS), .CONTROL_OUT(CONTROL));
  Board_2 Memory (
    .RESET(RESET), .CLK(CLK), .DATA_BUS_IN(DATA_BUS), .ADDRESS_BUS_IN(ADDRESS_BUS), .CONTROL_IN(CONTROL),
    .DATA_BUS_OUT(DATA_BUS), .ADDRESS_BUS_OUT(ADDRESS_BUS));
  Board_1 Clock_IO (
    .RESET(RESET), .DATA_BUS_IN(DATA_BUS), .ADDRESS_BUS_IN(ADDRESS_BUS), .CONTROL_IN(CONTROL), .CLK(CLK),
    .DATA_BUS_OUT(DATA_BUS));
  Pull_Resistor pull_resistor_1 (.node(ADDRESS_BUS));
  Pull_Resistor pull_resistor_2 (.node(DATA_BUS));
endmodule

module Board_1 (
  input  RESET,
  input  [7:0] DATA_BUS_IN,
  input  [15:0] ADDRESS_BUS_IN,
  input  [39:0] CONTROL_IN,
  output CLK,
  output [7:0] DATA_BUS_OUT
);

  wire and_2_out, and_3_out, and_4_out, and_5_out, and_6_out, and_7_out, and_8_out, and_9_out, clock_1_out,
       IO_0, IO_1, IO_2, IO_3, IO_4, IO_5, IO_6, IO_7, IO_8, IO_9, IO_10, IO_11, IO_12, IO_13, IO_14, IO_15;
  wire [6:0] keyboard_1_data;
  wire [7:0] IO_0_q, IO_1_q, IO_2_q, IO_3_q;
  wire [7:7] pull_resistor_1_node;

  Clock clock_1 (.out(clock_1_out));
  and and_1 (CLK, clock_1_out, ~CONTROL_IN[1]);  // AND_Gate
  and and_2 (and_2_out, ADDRESS_BUS_IN[8], ADDRESS_BUS_IN[9], ADDRESS_BUS_IN[10], ADDRESS_BUS_IN[11], ADDRESS_BUS_IN[12], ADDRESS_BUS_IN[13], ADDRESS_BUS_IN[14], ADDRESS_BUS_IN[15]);
  Decoder #(.select(4)) decoder_1 (
    .out0(IO_0), .out1(IO_1), .out2(IO_2), .out3(IO_3), .out4(IO_4), .out5(IO_5), .out6(IO_6), .out7(IO_7),
    .out8(IO_8), .out9(IO_9), .out10(IO_10), .out11(IO_11), .out12(IO_12), .out13(IO_13), .out14(IO_14),
    .out15(IO_15), .sel(ADDRESS_BUS_IN[3:0]), .en(and_2_out));
  and and_3 (and_3_out, IO_0, CONTROL_IN[35]);
  and and_4 (and_4_out, IO_1, CONTROL_IN[35]);
  and and_5 (and_5_out, IO_2, CONTROL_IN[36]);
  and and_6 (and_6_out, IO_3, CONTROL_IN[35]);
  Register #(.trigger("falling")) u_IO_0 (.D(DATA_BUS_IN), .en(and_3_out), .clk(CLK), .Q(IO_0_q), .clr(RESET));
  Register u_IO_1 (.D(DATA_BUS_IN), .en(and_4_out), .clk(CLK), .Q(IO_1_q), .clr(RESET));
  Register u_IO_2 (.D({pull_resistor_1_node[7], keyboard_1_data}), .en(and_5_out), .clk(CLK), .Q(IO_2_q), .clr(RESET));
  Register #(.trigger("falling")) u_IO_3 (.D(DATA_BUS_IN), .en(and_6_out), .clk(CLK), .Q(IO_3_q), .clr(RESET));
  // LedBar #(.inputtype("row")) ledbar_1: pin names not known; wires that end beside it: IO_0_q
  _7_Segment_Display u_7_segment_display_1 ();  // open: g, f, a, b, e, d, c, dp
  // BCD_to_7_Segment_decoder bcd_to_7_segment_decoder_1: pin names not known
  // Binary_to_BCD_converter #(.binvalue(8)) binary_to_bcd_converter_1: pin names not known; wires that end beside it: IO_3_q
  and and_7 (and_7_out, IO_1, CONTROL_IN[35], CLK);
  assign DATA_BUS_OUT = and_8_out ? IO_2_q : 8'bz;  // Controlled_Buffer controlled_buffer_1
  and and_8 (and_8_out, IO_2, CONTROL_IN[36]);
  _7_Segment_Display u_7_segment_display_2 ();  // open: g, f, a, b, e, d, c, dp
  // BCD_to_7_Segment_decoder bcd_to_7_segment_decoder_2: pin names not known
  TTY #(.trigger("falling")) tty_1 (.data(IO_1_q[6:0]), .clk(and_7_out), .we(1'b1));  // open: clr
  _7_Segment_Display u_7_segment_display_3 ();  // open: g, f, a, b, e, d, c, dp
  // BCD_to_7_Segment_decoder bcd_to_7_segment_decoder_3: pin names not known
  and and_9 (and_9_out, IO_2, CONTROL_IN[36], CLK);
  Keyboard #(.trigger("falling")) keyboard_1 (.clk(and_9_out), .re(1'b1), .data(keyboard_1_data));  // open: clr, avail
  Pull_Resistor pull_resistor_1 (.node({pull_resistor_1_node[7], keyboard_1_data}));

  // Other names for the same wires on the sheet: ADDRESS_IN[15:0] = ADDRESS_BUS_IN; HLT = CONTROL_IN[1];
  //   PCI = CONTROL_IN[2]; PCO = CONTROL_IN[3]; PCJ = CONTROL_IN[4]; SPI = CONTROL_IN[5]; SPO = CONTROL_IN[6];
  //   SPOA = CONTROL_IN[7]; AI = CONTROL_IN[8]; BI = CONTROL_IN[9]; BO = CONTROL_IN[10]; HI = CONTROL_IN[11];
  //   HO = CONTROL_IN[12]; LI = CONTROL_IN[13]; LO = CONTROL_IN[14]; HLO = CONTROL_IN[15]; HLI = CONTROL_IN[16];
  //   ARHI = CONTROL_IN[17]; ARHO = CONTROL_IN[18]; ARLI = CONTROL_IN[19]; ARLO = CONTROL_IN[20];
  //   ARHLO = CONTROL_IN[21]; ALUO = CONTROL_IN[22]; OPADD = CONTROL_IN[23]; OPSUB = CONTROL_IN[24];
  //   OPNOT = CONTROL_IN[25]; OPNAND = CONTROL_IN[26]; OPSR = CONTROL_IN[27]; ALUFI = CONTROL_IN[28];
  //   INCE = CONTROL_IN[29]; DEC = CONTROL_IN[30]; INCI = CONTROL_IN[31]; INCO = CONTROL_IN[32]; FI = CONTROL_IN[33];
  //   FO = CONTROL_IN[34]; MI = CONTROL_IN[35]; MO = CONTROL_IN[36]; INI = CONTROL_IN[37]; RAMSTART = CONTROL_IN[38];
  //   SPSTART = CONTROL_IN[39]; DATA_IN[7:0] = DATA_BUS_IN; DATA_OUT[7:0] = DATA_BUS_OUT

  // Notes on the sheet:
  //   Board 1 - Power, Clock, I/O
  //   CLOCK
  //   Interface decoder
endmodule

module Board_2 (
  input  RESET,
  input  CLK,
  input  [7:0] DATA_BUS_IN,
  input  [15:0] ADDRESS_BUS_IN,
  input  [39:0] CONTROL_IN,
  output [7:0] DATA_BUS_OUT,
  output [15:0] ADDRESS_BUS_OUT
);

  wire and_1_out, and_2_out, counter_1_carry, ENABLED, or_1_out, or_2_out, or_3_out;
  wire [7:0] H_q, L_q, multiplexer_1_out, multiplexer_2_out, multiplexer_3_out, ram_1_dout, register_1_q,
       rom_1_data;
  wire [15:0] counter_1_q, pull_resistor_1_node;

  nand nand_1 (ENABLED, ADDRESS_BUS_IN[8], ADDRESS_BUS_IN[9], ADDRESS_BUS_IN[10], ADDRESS_BUS_IN[11], ADDRESS_BUS_IN[12], ADDRESS_BUS_IN[13], ADDRESS_BUS_IN[14], ADDRESS_BUS_IN[15]);
  Counter #(.max('hffff), .width(16)) counter_1 (
    .clr(RESET), .load(CONTROL_IN[4]), .up(1'b1), .count(CONTROL_IN[2]), .clk(CLK), .D(ADDRESS_BUS_IN),
    .carry(counter_1_carry), .Q(counter_1_q));
  Pull_Resistor pull_resistor_1 (.node(pull_resistor_1_node));
  assign pull_resistor_1_node = ENABLED ? ADDRESS_BUS_IN : 16'bz;  // Controlled_Buffer controlled_buffer_1
  ROM #(.addrWidth(16)) rom_1 (.addr(pull_resistor_1_node), .data(rom_1_data));
  Pull_Resistor pull_resistor_2 (.node(counter_1_carry));
  or or_1 (or_1_out, pull_resistor_1_node[14], pull_resistor_1_node[15]);
  assign ADDRESS_BUS_OUT = CONTROL_IN[3] ? counter_1_q : 16'bz;  // Controlled_Buffer controlled_buffer_2
  Register #(.trigger("falling")) register_1 (
    .D(DATA_BUS_IN), .en(CONTROL_IN[5]), .clk(CLK), .Q(register_1_q), .clr(RESET));
  RAM #(.addrWidth(16)) ram_1 (
    .addr(pull_resistor_1_node), .we(and_1_out), .oe(CONTROL_IN[36]), .clk(CLK), .din(DATA_BUS_IN),
    .dout(ram_1_dout));
  and and_1 (and_1_out, or_1_out, CONTROL_IN[35]);
  Multiplexer #(.width(8)) multiplexer_1 (
    .in0(DATA_BUS_IN), .in1(ADDRESS_BUS_IN[15:8]), .out(multiplexer_1_out), .sel(CONTROL_IN[16]));
  or or_2 (or_2_out, CONTROL_IN[16], CONTROL_IN[11]);
  Multiplexer #(.width(8)) multiplexer_2 (
    .in0(DATA_BUS_IN), .in1(ADDRESS_BUS_IN[7:0]), .out(multiplexer_2_out), .sel(CONTROL_IN[16]));
  or or_3 (or_3_out, CONTROL_IN[16], CONTROL_IN[13]);
  Register #(.trigger("falling")) H (.D(multiplexer_1_out), .en(or_2_out), .clk(CLK), .Q(H_q), .clr(RESET));
  Register #(.trigger("falling")) L (.D(multiplexer_2_out), .en(or_3_out), .clk(CLK), .Q(L_q), .clr(RESET));
  assign DATA_BUS_OUT = CONTROL_IN[6] ? register_1_q : 8'bz;  // Controlled_Buffer controlled_buffer_3
  assign ADDRESS_BUS_OUT[7:0] = CONTROL_IN[7] ? register_1_q : 8'bz;  // Controlled_Buffer controlled_buffer_4
  assign DATA_BUS_OUT = CONTROL_IN[12] ? H_q : 8'bz;  // Controlled_Buffer controlled_buffer_5
  assign DATA_BUS_OUT = CONTROL_IN[14] ? L_q : 8'bz;  // Controlled_Buffer controlled_buffer_6
  Multiplexer #(.width(8)) multiplexer_3 (.in0(rom_1_data), .in1(ram_1_dout), .out(multiplexer_3_out), .sel(or_1_out));
  assign DATA_BUS_OUT = and_2_out ? multiplexer_3_out : 8'bz;  // Controlled_Buffer controlled_buffer_7
  and and_2 (and_2_out, CONTROL_IN[36], ENABLED);
  assign ADDRESS_BUS_OUT = CONTROL_IN[15] ? {H_q, L_q} : 16'bz;  // Controlled_Buffer controlled_buffer_8

  // Other names for the same wires on the sheet: ADDRESS_IN[15:0] = ADDRESS_BUS_IN;
  //   ADDRESS_OUT[15:0] = ADDRESS_BUS_OUT; HLT = CONTROL_IN[1]; PCI = CONTROL_IN[2]; PCO = CONTROL_IN[3];
  //   PCJ = CONTROL_IN[4]; SPI = CONTROL_IN[5]; SPO = CONTROL_IN[6]; SPOA = CONTROL_IN[7]; AI = CONTROL_IN[8];
  //   BI = CONTROL_IN[9]; BO = CONTROL_IN[10]; HI = CONTROL_IN[11]; HO = CONTROL_IN[12]; LI = CONTROL_IN[13];
  //   LO = CONTROL_IN[14]; HLO = CONTROL_IN[15]; HLI = CONTROL_IN[16]; ARHI = CONTROL_IN[17]; ARHO = CONTROL_IN[18];
  //   ARLI = CONTROL_IN[19]; ARLO = CONTROL_IN[20]; ARHLO = CONTROL_IN[21]; ALUO = CONTROL_IN[22];
  //   OPADD = CONTROL_IN[23]; OPSUB = CONTROL_IN[24]; OPNOT = CONTROL_IN[25]; OPNAND = CONTROL_IN[26];
  //   OPSR = CONTROL_IN[27]; ALUFI = CONTROL_IN[28]; INCE = CONTROL_IN[29]; DEC = CONTROL_IN[30];
  //   INCI = CONTROL_IN[31]; INCO = CONTROL_IN[32]; FI = CONTROL_IN[33]; FO = CONTROL_IN[34]; MI = CONTROL_IN[35];
  //   MO = CONTROL_IN[36]; INI = CONTROL_IN[37]; RAMSTART = CONTROL_IN[38]; SPSTART = CONTROL_IN[39];
  //   DATA_IN[7:0] = DATA_BUS_IN; DATA_OUT[7:0] = DATA_BUS_OUT

  // Notes on the sheet:
  //   contents of rom_1 (hex, n*v repeats v):
  //   9 ff 12 fe 32 3b fe 0 b fe 0 49 1 6a 0 93 43 fe 0 b fe 0 49 0 6a 0 93 9 32 12 fe 1 b fe 1 46 46 21 5
  //   3e 21 c8 12 fe 0 c fe 0 31 32 49 cd 6a 0 93 9 0 76 86 79 1 49 fe 9 2 6a 0 93 9 0 e0 9 3 5a 0 93 9 ff
  //   21 a 5a 0 58 9 4 52 0 93 19 a 31 14 62 0 64 9 5 52 0 93 9 14 a8 9 c8 b8 49 14 6a 0 93 9 f e0 9 0 b0
  //   9 1 e0 c0 d8 49 f 6a 0 93 9 a 92 0 87 52 0 90 21 5 5a 0 8f 92 0 87 98 9 7b e8 12 fe ff e8
  //   Program Counter
  //   Board 2 - Memory, Program Counter, Stack Pointer
  //   Memory
  //   Stack Pointer
  //   Memory registers
endmodule

module Board_3 (
  input  RESET,
  input  CLK,
  input  [7:0] DATA_BUS_IN,
  input  [15:0] ADDRESS_BUS_IN,
  input  [2:0] FLAGS_IN,
  output [7:0] DATA_BUS_OUT,
  output [15:0] ADDRESS_BUS_OUT,
  output [39:0] CONTROL_OUT
);

  wire or_1_out;
  wire [3:0] counter_1_q;
  wire [7:0] ARH_q, ARL_q, register_1_q;

  Register #(.trigger("falling")) register_1 (
    .D(DATA_BUS_IN), .en(CONTROL_OUT[37]), .clk(CLK), .Q(register_1_q), .clr(RESET));
  Counter #(.max('hf), .trigger("falling"), .width(4)) counter_1 (
    .clr(or_1_out), .load(1'b0), .up(1'b1), .clk(CLK), .Q(counter_1_q));  // open: count, D, carry
  or or_1 (or_1_out, RESET, CONTROL_OUT[0]);
  ROM #(.addrWidth(15), .dataWidth(40)) rom_1 (.addr({register_1_q, FLAGS_IN, counter_1_q}), .data(CONTROL_OUT));
  Register #(.trigger("falling")) ARH (.D(DATA_BUS_IN), .en(CONTROL_OUT[17]), .clk(CLK), .Q(ARH_q), .clr(RESET));
  Register #(.trigger("falling")) ARL (.D(DATA_BUS_IN), .en(CONTROL_OUT[19]), .clk(CLK), .Q(ARL_q), .clr(RESET));
  assign DATA_BUS_OUT = CONTROL_OUT[18] ? ARH_q : 8'bz;  // Controlled_Buffer controlled_buffer_1
  assign DATA_BUS_OUT = CONTROL_OUT[20] ? ARL_q : 8'bz;  // Controlled_Buffer controlled_buffer_2
  assign ADDRESS_BUS_OUT = CONTROL_OUT[21] ? {ARH_q, ARL_q} : 16'bz;  // Controlled_Buffer controlled_buffer_3
  assign ADDRESS_BUS_OUT[8] = CONTROL_OUT[39] ? CONTROL_OUT[39] : 1'bz;  // Controlled_Buffer controlled_buffer_4
  assign ADDRESS_BUS_OUT[14] = CONTROL_OUT[38] ? CONTROL_OUT[38] : 1'bz;  // Controlled_Buffer controlled_buffer_5

  // Other names for the same wires on the sheet: ADDRESS_IN[15:0] = ADDRESS_BUS_IN;
  //   ADDRESS_OUT[15:0] = ADDRESS_BUS_OUT; IEND = CONTROL_OUT[0]; HLT = CONTROL_OUT[1]; PCI = CONTROL_OUT[2];
  //   PCO = CONTROL_OUT[3]; PCJ = CONTROL_OUT[4]; SPI = CONTROL_OUT[5]; SPO = CONTROL_OUT[6]; SPOA = CONTROL_OUT[7];
  //   AI = CONTROL_OUT[8]; BI = CONTROL_OUT[9]; BO = CONTROL_OUT[10]; HI = CONTROL_OUT[11]; HO = CONTROL_OUT[12];
  //   LI = CONTROL_OUT[13]; LO = CONTROL_OUT[14]; HLO = CONTROL_OUT[15]; HLI = CONTROL_OUT[16];
  //   ARHI = CONTROL_OUT[17]; ARHO = CONTROL_OUT[18]; ARLI = CONTROL_OUT[19]; ARLO = CONTROL_OUT[20];
  //   ARHLO = CONTROL_OUT[21]; ALUO = CONTROL_OUT[22]; OPADD = CONTROL_OUT[23]; OPSUB = CONTROL_OUT[24];
  //   OPNOT = CONTROL_OUT[25]; OPNAND = CONTROL_OUT[26]; OPSR = CONTROL_OUT[27]; ALUFI = CONTROL_OUT[28];
  //   INCE = CONTROL_OUT[29]; DEC = CONTROL_OUT[30]; INCI = CONTROL_OUT[31]; INCO = CONTROL_OUT[32];
  //   FI = CONTROL_OUT[33]; FO = CONTROL_OUT[34]; MI = CONTROL_OUT[35]; MO = CONTROL_OUT[36]; INI = CONTROL_OUT[37];
  //   RAMSTART = CONTROL_OUT[38]; SPSTART = CONTROL_OUT[39]; DATA_IN[7:0] = DATA_BUS_IN; DATA_OUT[7:0] = DATA_BUS_OUT

  // Notes on the sheet:
  //   Instruction register
  //   Step counter
  //   contents of rom_1 (hex, n*v repeats v):
  //   3000000008 4 1 13*0 3000000008 4 1 13*0 3000000008 4 1 13*0 3000000008 4 1 13*0 3000000008 4 1 13*0
  //   3000000008 4 1 13*0 3000000008 4 1 13*0 3000000008 4 1 1037*0 3000000008 4 1000000108 4 1 11*0
  //   3000000008 4 1000000108 4 1 11*0 3000000008 4 1000000108 4 1 11*0 3000000008 4 1000000108 4 1 11*0
  //   3000000008 4 1000000108 4 1 11*0 3000000008 4 1000000108 4 1 11*0 3000000008 4 1000000108 4 1 11*0
  //   3000000008 4 1000000108 4 1 139*0 3000000008 4 1000020008 4 1000080008 4 1000200100 1 8*0 3000000008
  //   4 1000020008 4 1000080008 4 1000200100 1 8*0 3000000008 4 1000020008 4 1000080008 4 1000200100 1 8*0
  //   3000000008 4 1000020008 4 1000080008 4 1000200100 1 8*0 3000000008 4 1000020008 4 1000080008 4
  //   1000200100 1 8*0 3000000008 4 1000020008 4 1000080008 4 1000200100 1 8*0 3000000008 4 1000020008 4
  //   1000080008 4 1000200100 1 8*0 3000000008 4 1000020008 4 1000080008 4 1000200100 1 8*0 3000000008 4
  //   1000020008 4 1000080008 4 1000200800 80100000 120080000 1000202000 1000008100 1 4*0 3000000008 4
  //   1000020008 4 1000080008 4 1000200800 80100000 120080000 1000202000 1000008100 1 4*0 3000000008 4
  //   1000020008 4 1000080008 4 1000200800 80100000 120080000 1000202000 1000008100 1 4*0 3000000008 4
  //   1000020008 4 1000080008 4 1000200800 80100000 120080000 1000202000 1000008100 1 4*0 3000000008 4
  //   1000020008 4 1000080008 4 1000200800 80100000 120080000 80040000 120020000 1000202000 1000008100 1 0
  //   0 3000000008 4 1000020008 4 1000080008 4 1000200800 80100000 120080000 80040000 120020000 1000202000
  //   1000008100 1 0 0 3000000008 4 1000020008 4 1000080008 4 200800 80100000 120080000 80040000 120020000
  //   1000202000 1000008100 1 0 0 3000000008 4 1000020008 4 1000080008 4 1000200800 80100000 120080000
  //   80040000 120020000 1000202000 1000008100 1 0 0 3000000008 4 1000080008 4 5000200100 1 10*0
  //   3000000008 4 1000080008 4 5000200100 1 10*0 3000000008 4 1000080008 4 5000200100 1 10*0 3000000008 4
  //   1000080008 4 5000200100 1 10*0 3000000008 4 1000080008 4 5000200100 1 10*0 3000000008 4 1000080008 4
  //   5000200100 1 10*0 3000000008 4 1000080008 4 5000200100 1 10*0 3000000008 4 1000080008 4 5000200100 1
  //   522*0 3000000008 4 1000020008 4 1000080008 4 800600000 1 8*0 3000000008 4 1000020008 4 1000080008 4
  //   800600000 1 8*0 3000000008 4 1000020008 4 1000080008 4 800600000 1 8*0 3000000008 4 1000020008 4
  //   1000080008 4 800600000 1 8*0 3000000008 4 1000020008 4 1000080008 4 800600000 1 8*0 3000000008 4
  //   1000020008 4 1000080008 4 800600000 1 8*0 3000000008 4 1000020008 4 1000080008 4 800600000 1 8*0
  //   3000000008 4 1000020008 4 1000080008 4 800600000 1 136*0 3000000008 4 1000020008 4 1000080008 4
  //   1000200800 80100000 120080000 1000202000 800408000 1 4*0 3000000008 4 1000020008 4 1000080008 4
  //   1000200800 80100000 120080000 1000202000 800408000 1 4*0 3000000008 4 1000020008 4 1000080008 4
  //   1000200800 80100000 120080000 1000202000 800408000 1 4*0 3000000008 4 1000020008 4 1000080008 4
  //   1000200800 80100000 120080000 1000202000 800408000 1 4*0 3000000008 4 1000020008 4 1000080008 4
  //   1000200800 80100000 120080000 80040000 120020000 1000202000 800408000 1 0 0 3000000008 4 1000020008
  //   4 1000080008 4 1000200800 80100000 120080000 80040000 120020000 1000202000 800408000 1 0 0
  //   3000000008 4 1000020008 4 1000080008 4 1000200800 80100000 120080000 80040000 120020000 1000202000
  //   800408000 1 0 0 3000000008 4 1000020008 4 1000080008 4 1000200800 80100000 120080000 80040000
  //   120020000 1000202000 800408000 1 0 0 3000000008 4 1000080008 4 4800600000 1 10*0 3000000008 4
  //   1000080008 4 4800600000 1 10*0 3000000008 4 1000080008 4 4800600000 1 10*0 3000000008 4 1000080008 4
  //   4800600000 1 10*0 3000000008 4 1000080008 4 4800600000 1 10*0 3000000008 4 1000080008 4 4800600000 1
  //   10*0 3000000008 4 1000080008 4 4800600000 1 10*0 3000000008 4 1000080008 4 4800600000 1 394*0
  //   3000000008 4 1000000208 4 10c00100 1 10*0 3000000008 4 1000000208 4 10c00100 1 10*0 3000000008 4
  //   1000000208 4 10c00100 1 10*0 3000000008 4 1000000208 4 10c00100 1 10*0 3000000008 4 1000000208 4
  //   10c00100 1 10*0 3000000008 4 1000000208 4 10c00100 1 10*0 3000000008 4 1000000208 4 10c0010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
  //   Board 3 - Control logic, Argument registers
  //   Argument registers
  //   Microcode
  //   Address injection
endmodule

module Board_4 (
  input  RESET,
  input  CLK,
  input  [7:0] DATA_BUS_IN,
  input  [15:0] ADDRESS_BUS_IN,
  input  [39:0] CONTROL_IN,
  output [7:0] DATA_BUS_OUT,
  output [15:0] ADDRESS_BUS_OUT,
  output [2:0] CONTROL_FLAGS_OUT
);

  wire adder_1_cout, ALUFS, and_1_out, and_2_out, and_3_out, and_4_out, counter_1_carry, d_ff_1_q,
       FLAG_OVERFLOW_IN, FLAG_SIGN_IN, FLAG_WRAP_IN, FLAG_ZERO_IN, nor_1_out, not_1_out, not_4_out, or_1_out,
       or_2_out, or_5_out, xor_1_out;
  wire [3:0] multiplexer_3_out;
  wire [3:2] F_q;
  wire [6:0] multiplexer_2_out;
  wire [7:0] A_q, adder_1_out, B_q, controlled_buffer_3_out, counter_1_q, multiplexer_1_out, nand_1_out,
       not_2_out, not_3_out;

  Register #(.trigger("falling")) A (.D(DATA_BUS_IN), .en(CONTROL_IN[8]), .clk(CLK), .Q(A_q), .clr(RESET));
  Register #(.trigger("falling")) B (.D(DATA_BUS_IN), .en(CONTROL_IN[9]), .clk(CLK), .Q(B_q), .clr(RESET));
  assign DATA_BUS_OUT = CONTROL_IN[10] ? B_q : 8'bz;  // Controlled_Buffer controlled_buffer_1
  Counter counter_1 (
    .clr(RESET), .load(CONTROL_IN[31]), .up(not_1_out), .count(CONTROL_IN[29]), .clk(CLK), .D(DATA_BUS_IN),
    .carry(counter_1_carry), .Q(counter_1_q));
  not not_1 (not_1_out, CONTROL_IN[30]);
  // Probe on A_q
  // Probe on B_q
  and and_1 (and_1_out, CONTROL_FLAGS_OUT[0], CONTROL_IN[28]);
  assign not_2_out = ~B_q;  // NOT_Gate not_2, 8 bits wide
  or or_1 (or_1_out, CONTROL_IN[23], CONTROL_IN[24]);
  nor nor_1 (nor_1_out, CONTROL_IN[25], CONTROL_IN[26], CONTROL_IN[23], CONTROL_IN[24], CONTROL_IN[27]);
  assign nand_1_out = ~(A_q & B_q);  // NAND_Gate nand_1, 8 bits wide
  xor xor_1 (xor_1_out, and_1_out, CONTROL_IN[24]);
  Multiplexer #(.width(8)) multiplexer_1 (.in0(B_q), .in1(not_2_out), .out(multiplexer_1_out), .sel(CONTROL_IN[24]));
  assign DATA_BUS_OUT = CONTROL_IN[32] ? counter_1_q : 8'bz;  // Controlled_Buffer controlled_buffer_2
  assign controlled_buffer_3_out = nor_1_out ? A_q : 8'bz;  // Controlled_Buffer controlled_buffer_3
  assign controlled_buffer_3_out = CONTROL_IN[26] ? nand_1_out : 8'bz;  // Controlled_Buffer controlled_buffer_4
  assign controlled_buffer_3_out = CONTROL_IN[27] ? {1'b0, A_q[7:1]} : 8'bz;  // Controlled_Buffer controlled_buffer_5
  assign controlled_buffer_3_out = or_1_out ? adder_1_out : 8'bz;  // Controlled_Buffer controlled_buffer_6
  Adder adder_1 (.a(A_q), .b(multiplexer_1_out), .out(adder_1_out), .cin(xor_1_out), .cout(adder_1_cout));
  D_Flip_Flop d_ff_1 (.D(counter_1_carry), .clk(and_2_out), .Q(d_ff_1_q), .reset(RESET));  // open: Qn, preset
  and and_2 (and_2_out, CLK, CONTROL_IN[29]);
  Pull_Resistor pull_resistor_1 (.node(controlled_buffer_3_out));
  and and_3 (and_3_out, A_q[0], CONTROL_IN[27]);
  and and_4 (and_4_out, adder_1_cout, or_2_out);
  or or_2 (or_2_out, CONTROL_IN[23], CONTROL_IN[24]);
  Multiplexer #(.width(8)) multiplexer_2 (
    .in0(controlled_buffer_3_out), .in1(not_3_out), .out({FLAG_SIGN_IN, multiplexer_2_out}),
    .sel(CONTROL_IN[25]));
  assign not_3_out = ~controlled_buffer_3_out;  // NOT_Gate not_3, 8 bits wide
  or or_3 (FLAG_WRAP_IN, and_3_out, and_4_out);
  D_Flip_Flop #(.trigger("falling")) INC_WRAP (
    .D(d_ff_1_q), .clk(and_2_out), .Q(CONTROL_FLAGS_OUT[2]), .reset(RESET));  // open: Qn, preset
  assign DATA_BUS_OUT = CONTROL_IN[22] ? {FLAG_SIGN_IN, multiplexer_2_out} : 8'bz;  // Controlled_Buffer controlled_buffer_7
  // Probe on DATA_BUS_OUT
  xor xor_2 (FLAG_OVERFLOW_IN, A_q[7], FLAG_SIGN_IN);
  nor nor_2 (FLAG_ZERO_IN, FLAG_SIGN_IN, multiplexer_2_out[6], multiplexer_2_out[5], multiplexer_2_out[4], multiplexer_2_out[3], multiplexer_2_out[2], multiplexer_2_out[1], multiplexer_2_out[0]);
  or or_4 (ALUFS, CONTROL_IN[25], CONTROL_IN[26], CONTROL_IN[23], CONTROL_IN[24], CONTROL_IN[27]);
  not not_4 (not_4_out, CONTROL_IN[33]);
  Multiplexer #(.width(4)) multiplexer_3 (
    .in0(DATA_BUS_IN[3:0]), .in1({FLAG_OVERFLOW_IN, FLAG_SIGN_IN, FLAG_ZERO_IN, FLAG_WRAP_IN}),
    .out(multiplexer_3_out), .sel(not_4_out));
  or or_5 (or_5_out, CONTROL_IN[33], ALUFS);
  Register #(.trigger("falling"), .width(4)) F (
    .D(multiplexer_3_out), .en(or_5_out), .clk(CLK), .Q({F_q, CONTROL_FLAGS_OUT[1:0]}), .clr(RESET));
  assign DATA_BUS_OUT[3:0] = CONTROL_IN[34] ? {F_q, CONTROL_FLAGS_OUT[1:0]} : 4'bz;  // Controlled_Buffer controlled_buffer_8

  // Other names for the same wires on the sheet: FLAG_WRAP_OUT = CONTROL_FLAGS_OUT[0];
  //   FLAG_ZERO_OUT = CONTROL_FLAGS_OUT[1]; ADDRESS_IN[15:0] = ADDRESS_BUS_IN; ADDRESS_OUT[15:0] = ADDRESS_BUS_OUT;
  //   INC_FLAG_WRAP_IN = CONTROL_FLAGS_OUT[2]; HLT = CONTROL_IN[1]; PCI = CONTROL_IN[2]; PCO = CONTROL_IN[3];
  //   PCJ = CONTROL_IN[4]; SPI = CONTROL_IN[5]; SPO = CONTROL_IN[6]; SPOA = CONTROL_IN[7]; AI = CONTROL_IN[8];
  //   BI = CONTROL_IN[9]; BO = CONTROL_IN[10]; HI = CONTROL_IN[11]; HO = CONTROL_IN[12]; LI = CONTROL_IN[13];
  //   LO = CONTROL_IN[14]; HLO = CONTROL_IN[15]; HLI = CONTROL_IN[16]; ARHI = CONTROL_IN[17]; ARHO = CONTROL_IN[18];
  //   ARLI = CONTROL_IN[19]; ARLO = CONTROL_IN[20]; ARHLO = CONTROL_IN[21]; ALUO = CONTROL_IN[22];
  //   OPADD = CONTROL_IN[23]; OPSUB = CONTROL_IN[24]; OPNOT = CONTROL_IN[25]; OPNAND = CONTROL_IN[26];
  //   OPSR = CONTROL_IN[27]; ALUFI = CONTROL_IN[28]; INCE = CONTROL_IN[29]; DEC = CONTROL_IN[30];
  //   INCI = CONTROL_IN[31]; INCO = CONTROL_IN[32]; FI = CONTROL_IN[33]; FO = CONTROL_IN[34]; MI = CONTROL_IN[35];
  //   MO = CONTROL_IN[36]; INI = CONTROL_IN[37]; RAMSTART = CONTROL_IN[38]; SPSTART = CONTROL_IN[39];
  //   DATA_IN[7:0] = DATA_BUS_IN; DATA_OUT[7:0] = DATA_BUS_OUT

  // Notes on the sheet:
  //   Board 4 - ALU
  //   ALU registers
  //   Incrementer
  //   ALU
  //   DEFAULT
  //   NAND
  //   SHIFT RIGHT
  //   ADD/SUBTRACT
  //   NOT
  //   ALU flags
endmodule
